# Fritzing sketch Morse Code (saved by Fritzing 0.9.3b)
breadboards: 1

parts:
  Beeper = Piezo Speaker
  Push/Pull_Button = SWITCH-MOMENTARY-2 [package=tactile-pth]
  Arduino_Uno = Arduino Uno (Rev3)
  LCD_(16*2) = DeuLigne 1.1 - The Snootlab's LCD shield for Arduino
  R1 = Resistor [tolerance=±5% resistance=220 package="2010 [SMD]"]
  VCC = Battery block 9V

nets:
  GND: Beeper.pin1, Arduino_Uno.D9_PWM, Arduino_Uno.GND, LCD_(16*2).GND, R1.Pin_1, VCC.-
  N1: Beeper.pin2, Arduino_Uno.D8
  N2: Push/Pull_Button.1, R1.Pin_0
  5V: Push/Pull_Button.2, Arduino_Uno.5V, Arduino_Uno.VIN, LCD_(16*2).+5V, VCC.+
  N3: Arduino_Uno.D0/RX, LCD_(16*2).D0_RX
  N4: Arduino_Uno.D1/TX, LCD_(16*2).D1_TX
  N5: Arduino_Uno.D2, LCD_(16*2).D2
  N6: Arduino_Uno.D3_PWM, LCD_(16*2).D3
  N7: Arduino_Uno.D4, LCD_(16*2).D4
  N8: Arduino_Uno.D5_PWM, LCD_(16*2).D5
  N9: Arduino_Uno.D6_PWM, LCD_(16*2).D6
  N10: Arduino_Uno.D7, LCD_(16*2).D7
